# Fritzing sketch bmp-180 (saved by Fritzing 0.9.0b)
breadboards: 1

parts:
  Part1 = Intel Galileo
  Part2 = Barometric Pressure Sensor - BMP085 Breakout

nets:
  N1: Part1.A4/SDA, Part2.VCC
  N2: Part1.A5/SCL, Part2.GND
  N3: Part1.GND, Part2.EOC

notes:
  +3,5 V
  GND
  BMP-180 - Pressure
  https://learn.sparkfun.com/tutorials/bmp180-barometric-pressure-sensor-hookup-
