# Fritzing sketch ml8511 (saved by Fritzing 0.9.0b)
breadboards: 1

parts:
  Part1 = Intel Galileo
  PART1 = ML8511 UV Sensor Breakout [part_number=SEN-12705]  # not connected

nets:
  N1: Part1.A4/SDA, Part1.3V3

notes:
  +3,5 V
  GND
  ML-8511 - UV Sensor
  https://learn.sparkfun.com/tutorials/ml8511-uv-sensor-hookup-guide/using-the-ml8511

custom parts:
  ML8511 UV Sensor Breakout: Description: The ML8511 breakout is an easy to use ultraviolet light sensor. The MP8511 UV Sensor works by outputing an analog signal in relation to the amount of UV light it detects. This breakout can be very handy in creating devices that warn the user of sunburn or detect the UV index as it relates to weather conditions. This sensor breakout can detect 280-390nm light most effectively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
