# Fritzing sketch simple_led (saved by Fritzing 0.9.0b)
breadboards: 1

parts:
  Part1 = Intel Galileo
  LED1 = LED - 5mm [color="Red (633nm)" package="5 mm [THT]"]
  LED2 = LED - 5mm [color="Red (633nm)" package="5 mm [THT]"]

nets:
  N1: Part1.GND, LED1.cathode, LED2.cathode
  N2: Part1.D2, LED2.anode
  N3: Part1.D4, LED1.anode
